# Fritzing sketch WeaverCircuitDiagram (saved by Fritzing 0.8.7b)
breadboards: 1

parts:
  Teensy_LC = Teensy 3.1  # not connected
  8-10_V_DC = Power plug
  A4988 = A4988 Stepper Motor Driver Carrier  # not connected
  C1 = Electrolytic Capacitor [capacitance=100µF package="200 mil [THT, electrolytic]"]
  Attach_Canvas_here = Stepper Motor - Bipolar  # not connected

nets:
  N1: 8-10_V_DC.GND, C1.-
  N2: 8-10_V_DC.VCC, C1.+
